// Logisim project Logisim circuit file of 7 segment display.circ as structural Verilog: 3 circuits, main circuit 7 bar Combinational circuit
module Digit_with_7_segment_display (
  input  w,
  input  x,
  input  y,
  input  z
);

  wire _7_bar_comb_circ_a, _7_bar_comb_circ_b, _7_bar_comb_circ_c, _7_bar_comb_circ_d, _7_bar_comb_circ_e,
       _7_bar_comb_circ_f, _7_bar_comb_circ_g;

  _7_bar_Combinational_circuit _7_bar_comb_circ (
    .w(w), .x(x), .y(y), .z(z), .a(_7_bar_comb_circ_a), .b(_7_bar_comb_circ_b), .c(_7_bar_comb_circ_c),
    .d(_7_bar_comb_circ_d), .e(_7_bar_comb_circ_e), .f(_7_bar_comb_circ_f), .g(_7_bar_comb_circ_g));
  _7_Segment_Display u_7_segment_display_1 (
    .g(_7_bar_comb_circ_f), .f(_7_bar_comb_circ_a), .a(_7_bar_comb_circ_e), .b(_7_bar_comb_circ_c),
    .e(_7_bar_comb_circ_b), .d(_7_bar_comb_circ_g), .c(_7_bar_comb_circ_d));  // open: dp

  // Notes on the sheet:
  //   a
  //   b
  //   c
  //   e
  //   f
  //   g
  //   d
  //   VALID INPUTS are only between 0-9, inclusive, 0000-1001
  //   a
  //   f
  //   c
  //   e
  //   b
  //   d
  //   g
endmodule

module Digit_with_LED_lights (
  input  w,
  input  x,
  input  y,
  input  z
);

  wire _7_bar_comb_circ_a, _7_bar_comb_circ_b, _7_bar_comb_circ_c, _7_bar_comb_circ_d, _7_bar_comb_circ_e,
       _7_bar_comb_circ_f, _7_bar_comb_circ_g;

  _7_bar_Combinational_circuit _7_bar_comb_circ (
    .w(w), .x(x), .y(y), .z(z), .a(_7_bar_comb_circ_a), .b(_7_bar_comb_circ_b), .c(_7_bar_comb_circ_c),
    .d(_7_bar_comb_circ_d), .e(_7_bar_comb_circ_e), .f(_7_bar_comb_circ_f), .g(_7_bar_comb_circ_g));
  LED led_1 (.in(_7_bar_comb_circ_e));
  LED led_2 (.in(_7_bar_comb_circ_e));
  LED led_3 (.in(_7_bar_comb_circ_a));
  LED led_4 (.in(_7_bar_comb_circ_a));
  LED led_5 (.in(_7_bar_comb_circ_a));
  LED led_6 (.in(_7_bar_comb_circ_a));
  LED led_7 (.in(_7_bar_comb_circ_f));
  LED led_8 (.in(_7_bar_comb_circ_f));
  LED led_9 (.in(_7_bar_comb_circ_b));
  LED led_10 (.in(_7_bar_comb_circ_b));
  LED led_11 (.in(_7_bar_comb_circ_b));
  LED led_12 (.in(_7_bar_comb_circ_b));
  LED led_13 (.in(_7_bar_comb_circ_g));
  LED led_14 (.in(_7_bar_comb_circ_g));
  LED led_15 (.in(_7_bar_comb_circ_e));
  LED led_16 (.in(_7_bar_comb_circ_c));
  LED led_17 (.in(_7_bar_comb_circ_c));
  LED led_18 (.in(_7_bar_comb_circ_c));
  LED led_19 (.in(_7_bar_comb_circ_c));
  LED led_20 (.in(_7_bar_comb_circ_f));
  LED led_21 (.in(_7_bar_comb_circ_d));
  LED led_22 (.in(_7_bar_comb_circ_d));
  LED led_23 (.in(_7_bar_comb_circ_d));
  LED led_24 (.in(_7_bar_comb_circ_d));
  LED led_25 (.in(_7_bar_comb_circ_g));

  // Notes on the sheet:
  //   a
  //   b
  //   g
  //   VALID INPUTS are only between 0-9, inclusive, 0000-1001
  //   c
  //   d
  //   e
  //   f
  //   e
  //   a
  //   f
  //   b
  //   g
  //   c
  //   d
endmodule

// COMB circ
module _7_bar_Combinational_circuit (
  input  w,
  input  x,
  input  y,
  input  z,
  output a,
  output b,
  output c,
  output d,
  output e,
  output f,
  output g
);

  wire not_1_out, not_2_out, not_3_out, not_4_out, w_y_out, x_prime_w_y_out, x_prime_y_2_out, x_prime_y_out,
       x_prime_z_prime_out, x_y_prime_z_prime_out, xy_prime_z_out, xz_out, y_prime_z_prime_2_out,
       y_prime_z_prime_out, yz_out;

  not not_1 (not_1_out, w);
  not not_2 (not_2_out, x);
  not not_3 (not_3_out, y);
  not not_4 (not_4_out, z);
  and y_prime_z_prime (y_prime_z_prime_out, not_3_out, not_4_out);
  or y_prime_z_prime_2 (y_prime_z_prime_2_out, not_3_out, not_4_out);
  or x_prime_y (x_prime_y_out, not_2_out, y);
  and yz (yz_out, y, z);
  and xz (xz_out, x, z);
  and x_prime_z_prime (x_prime_z_prime_out, not_2_out, not_4_out);
  and x_prime_y_2 (x_prime_y_2_out, not_2_out, y);
  or w_y (w_y_out, w, y);
  and xy_prime_z (xy_prime_z_out, x, not_3_out, z);
  and x_y_prime_z_prime (x_y_prime_z_prime_out, y_prime_z_prime_2_out, x);
  and x_prime_y_z_prime (b, x_prime_y_out, not_4_out);
  and x_prime_w_y (x_prime_w_y_out, w_y_out, not_2_out);
  or or_1 (a, w, y_prime_z_prime_out, x_y_prime_z_prime_out);
  or or_2 (g, x_prime_w_y_out, b, xy_prime_z_out);
  or or_3 (c, not_2_out, yz_out, y_prime_z_prime_out);
  or or_4 (d, w, x, not_3_out, z);
  or or_5 (e, w, y, xz_out, x_prime_z_prime_out);
  or or_6 (f, w, x_y_prime_z_prime_out, x_prime_y_2_out);

  // Notes on the sheet:
  //   w
  //   w
  //   w
  //   w
  //   w
  //   w'
  //   x'
  //   x
  //   x'
  //   w'
  //   x
  //   x'
  //   w'
  //   x
  //   w'
  //   x'
  //   x
  //   w'
  //   x
  //   x'
  //   VALID INPUTS are only between 0-9, inclusive, 0000-1001
  //   y
  //   y'
  //   z'
  //   z
  //   y
  //   y'
  //   z
  //   z'
  //   y
  //   y'
  //   z
  //   z'
  //   y'
  //   y
  //   z'
  //   z
  //   y'
  //   y
  //   z
  //   z'
endmodule
